# Fritzing sketch ti30s_v7s2 (saved by Fritzing 0.9.1b)
circuit board: 4.99999cm x 9.00001cm
breadboards: 1

parts:
  LED1 = IC, DIP package, 12 pins [chip_label=IC]
  LED2 = IC, DIP package, 12 pins [chip_label=IC]
  LED3 = IC, DIP package, 12 pins [chip_label=IC]
  1X = Pushbutton [package=THT]
  3X = Pushbutton [package=THT]
  4X = Pushbutton [package=THT]
  8X = Pushbutton [package=THT]
  8Y = Pushbutton [package=THT]
  1Y = Pushbutton [package=THT]
  7Y = Pushbutton [package=THT]
  4Y = Pushbutton [package=THT]
  3Y = Pushbutton [package=THT]
  AY = Pushbutton [package=THT]
  1Z = Pushbutton [package=THT]
  7X = Pushbutton [package=THT]
  AX = Pushbutton [package=THT]
  4Z = Pushbutton [package=THT]
  7Z = Pushbutton [package=THT]
  5Z = Pushbutton [package=THT]
  AZ = Pushbutton [package=THT]
  5Y = Pushbutton [package=THT]
  2Z = Pushbutton [package=THT]
  BZ = Pushbutton [package=THT]
  9Z = Pushbutton [package=THT]
  0Z = Pushbutton [package=THT]
  BY = Pushbutton [package=THT]
  0X = Pushbutton [package=THT]
  9X = Pushbutton [package=THT]
  0Y = Pushbutton [package=THT]
  BX = Pushbutton [package=THT]
  9Y = Pushbutton [package=THT]
  2Y = Pushbutton [package=THT]
  2X = Pushbutton [package=THT]
  [1k] = female pin header, 1 pin [form="♀ (female)"]
  J11 = female pin header, 1 pin [form="♀ (female)"]
  102 = female pin header, 1 pin [form="♀ (female)"]
  J4 = female pin header, 1 pin [form="♀ (female)"]
  [47k] = female pin header, 1 pin [form="♀ (female)"]
  J6 = female pin header, 1 pin [form="♀ (female)"]
  | = female pin header, 1 pin [form="♀ (female)"]
  104 = female pin header, 1 pin [form="♀ (female)"]
  3Z = Pushbutton [package=THT]
  OFF = female pin header, 3 pins [form="♀ (female)"]
  Pad1 = Pad [width=2 height=5 connect=center]
  Pad2 = Pad [width=2 height=6 connect=center]
  msp431 = IC, DIP package, 20 pins [chip_label=IC]
  164 = IC, DIP package, 14 pins [chip_label=IC]
  8Z = Pushbutton [package=THT]
  T_R_G = female pin header, 3 pins [form="♀ (female)"]

nets:
  N1: LED1.pin1, 0Z.leg1, 0X.leg1, 0Y.leg1, msp431.pin19
  N2: LED1.pin2, LED2.pin2, LED3.pin2, 164.pin5
  N3: LED1.pin3, LED2.pin3, LED3.pin3, 164.pin4
  N4: LED1.pin4, 2Z.leg1, 2Y.leg1, 2X.leg1, msp431.pin18
  N5: LED1.pin5, LED2.pin5, LED3.pin5, 164.pin3
  N6: LED1.pin6, 3X.leg1, 3Y.leg0, 3Z.leg0, msp431.pin3
  N7: LED1.pin7, LED2.pin7, LED3.pin7, 164.pin6
  N8: LED1.pin8, LED2.pin8, LED3.pin8, 164.pin13
  N9: LED1.pin9, LED2.pin9, LED3.pin9, 164.pin12
  N10: LED1.pin10, 1X.leg0, 1Y.leg0, 1Z.leg0, msp431.pin2
  N11: LED1.pin11, LED2.pin11, LED3.pin11, 164.pin11
  N12: LED1.pin12, LED2.pin12, LED3.pin12, 164.pin10
  N13: LED2.pin1, 4X.leg0, 4Y.leg0, 4Z.leg0, msp431.pin4
  N14: LED2.pin4, msp431.pin8
  N15: LED2.pin6, 7Y.leg0, 7X.leg0, 7Z.leg0, msp431.pin6
  N16: LED2.pin10, 5Z.leg0, 5Y.leg0, msp431.pin5
  N17: LED3.pin1, 8X.leg1, 8Y.leg0, msp431.pin7, 8Z.leg0
  N18: LED3.pin4, AY.leg0, AX.leg0, AZ.leg0, msp431.pin14
  N19: LED3.pin6, BZ.leg1, BY.leg1, BX.leg1, msp431.pin15
  N20: LED3.pin10, 9Z.leg1, 9X.leg1, 9Y.leg1, msp431.pin9
  N21: 1X.leg1, 3X.leg0, 4X.leg1, 8X.leg0, 7X.leg1, AX.leg1, 0X.leg0, 9X.leg0, BX.leg0, 2X.leg0, msp431.pin13
  N22: 8Y.leg1, 1Y.leg1, 7Y.leg1, 4Y.leg1, 3Y.leg1, AY.leg1, 5Y.leg1, BY.leg0, 0Y.leg0, 9Y.leg0, 2Y.leg0, msp431.pin12
  N23: 1Z.leg1, 4Z.leg1, 7Z.leg1, 5Z.leg1, AZ.leg1, 2Z.leg0, BZ.leg0, 9Z.leg0, 0Z.leg0, 3Z.leg1, msp431.pin11, 8Z.leg1
  N24: [1k].pin1, J4.pin1, 164.pin1, 164.pin2
  N25: J11.pin1, msp431.pin10, 164.pin8
  N26: 102.pin1, 104.pin1, Pad2.pad, msp431.pin20, 164.pin7, T_R_G.pin3
  N27: [47k].pin1, msp431.pin16, T_R_G.pin2
  N28: J6.pin1, |.pin1, OFF.pin2, msp431.pin1, 164.pin9, 164.pin14
  N29: OFF.pin1, Pad1.pad
  N30: msp431.pin17, T_R_G.pin1

notes:
  1 e c 3 h 4
  a b 2 f d g
  ON
  PGM        RUN
  HP woodstock / spice microcode emulation
  SST   BST   GTO
  1   2   3
  0
  ÷
  .
  R/S
  4   5   6
  7   8   9
  +
  -
  g
  f
  ENTER    CHS   EEX   CLS
  X~Y    R    STO   RCL     +
  ×
  X=Y     -H.MS     LASTX    PAUSE
  X=0       -H        PI      NOP
  X!Y       INT     sqrtX       yX
  X!0      FRAC       X²      ABS
  X>Y       sin       cos      tan
  X>0       arc       arc      arc
  X<Y        ln       log       >R
  X<0        ex       10x       >P
  clr──PREFIX────PRGM────REG────STK─
  x       s                     -
  %     1/x
  ──deg──────rad───────grd─
  FIX    SCI    ENG
  www.simpleavr.com
  see nonpareil.brouhaha.com
  based on Eric Smith and other's work
  please observe GNU license on firmware
  source usually resides in github/simpleavr
  chris chung february 2015 b4
  NP-25  V3
  _
  M
  »

custom parts:
  Pushbutton: A generic pushbutton.
